# Fritzing sketch ESP_Relay (saved by Fritzing 0.9.2b)
circuit board: 4.59149cm x 3.07501cm
breadboards: 1

parts:
  NodeMCU_V1_0 = NodeMCU V1.0
  R5 = Trimmer Potentiometer [maximum_resistance=10kΩ package=THT]
  Q2 = NPN-Transistor [package="TO92 [THT]"]
  Q3 = NPN-Transistor [package="TO92 [THT]"]
  Q4 = NPN-Transistor [package="TO92 [THT]"]
  Q1 = NPN-Transistor [package="TO92 [THT]"]
  OUT = male pin header, 6 pins [form="♂ (male)"]
  R4 = Resistor [tolerance=±5% resistance=2.2k package="2010 [SMD]"]
  R3 = Resistor [tolerance=±5% resistance=2.2k package="2010 [SMD]"]
  R2 = Resistor [tolerance=±5% resistance=2.2k package="2010 [SMD]"]
  R1 = Resistor [tolerance=±5% resistance=2.2k package="2010 [SMD]"]
  ACS = male pin header, 3 pins [form="♂ (male)"]
  PS = male pin header, 5 pins [form="♂ (male)"]
  Header1 = male pin header, 15 pins [form="♂ (male)"]
  Header2 = male pin header, 15 pins [form="♂ (male)"]

nets:
  N1: NodeMCU_V1_0.D0, R1.Pin_0, Header1.pin1
  N2: NodeMCU_V1_0.D1, R2.Pin_0, Header1.pin2
  N3: NodeMCU_V1_0.D2, R3.Pin_0, Header1.pin3
  N4: NodeMCU_V1_0.D3, R4.Pin_0, Header1.pin4
  N5: NodeMCU_V1_0.D4, Header1.pin5
  N6: NodeMCU_V1_0.3V3, Header1.pin6, Header1.pin15, Header2.pin5
  GND: NodeMCU_V1_0.GND, R5.leg1, Q2.E, Q3.E, Q4.E, Q1.E, OUT.pin1, ACS.pin3, PS.pin5, Header1.pin7, Header1.pin14, Header2.pin2, Header2.pin6
  N7: NodeMCU_V1_0.D5, Header1.pin8
  N8: NodeMCU_V1_0.D6, Header1.pin9
  N9: NodeMCU_V1_0.D7, Header1.pin10
  N10: NodeMCU_V1_0.D8, Header1.pin11
  N11: NodeMCU_V1_0.RX, Header1.pin12
  N12: NodeMCU_V1_0.TX, Header1.pin13
  5V: NodeMCU_V1_0.Vin, OUT.pin6, ACS.pin1, PS.pin3, Header2.pin1
  N13: NodeMCU_V1_0.RST, Header2.pin3
  N14: NodeMCU_V1_0.EN, Header2.pin4
  N15: NodeMCU_V1_0.CLK, Header2.pin7
  N16: NodeMCU_V1_0.SD0, Header2.pin8
  N17: NodeMCU_V1_0.CMD, Header2.pin9
  N18: NodeMCU_V1_0.SD1, Header2.pin10
  N19: NodeMCU_V1_0.SD2, Header2.pin11
  N20: NodeMCU_V1_0.SD3, Header2.pin12
  N21: NodeMCU_V1_0.RSV#40, Header2.pin13
  N22: NodeMCU_V1_0.RSV#41, Header2.pin14
  N23: NodeMCU_V1_0.A0, R5.wiper, Header2.pin15
  N24: R5.leg2, ACS.pin2
  N25: Q2.B, R2.Pin_1
  N26: Q2.C, OUT.pin3
  N27: Q3.B, R3.Pin_1
  N28: Q3.C, OUT.pin4
  N29: Q4.B, R4.Pin_1
  N30: Q4.C, OUT.pin5
  N31: Q1.B, R1.Pin_1
  N32: Q1.C, OUT.pin2
  30V: PS.pin1
  1.8V: PS.pin2
  3.3V: PS.pin4

notes:
  D0
  A0
  GND
  3.3V
  5V
  1.8V
  30V
  VCC
  VOUT
  Relay

custom parts:
  NodeMCU V1.0: ESP8266 based NodeMCU
